# Fritzing sketch easy_race_lap_timer_raspberry_2_sensor_shield_rev1 (saved by Fritzing 0.9.2b)
circuit board: 6.10266cm x 2.50811cm
breadboards: 1

parts:
  J1 = shrouded pin header, 40 pins [form="♂ (shrouded male)"]
  Pad1 = Pad [width=3.38803615101437 height=3.79345389117291 connect=center]
  Pad2 = Pad [width=3.38803615101437 height=3.79345389117291 connect=center]
  Pad3 = Pad [width=3.38803615101437 height=3.79345389117291 connect=center]
  Pad5 = Pad [width=3.38803615101437 height=3.79345389117291 connect=center]
  Pad6 = Pad [width=3.38803615101437 height=3.79345389117291 connect=center]
  Pad7 = Pad [width=3.38803615101437 height=3.79345389117291 connect=center]
  Pad9 = Pad [width=3.38803615101437 height=3.79345389117291 connect=center]
  Pad10 = Pad [width=3.38803615101437 height=3.79345389117291 connect=center]
  Pad11 = Pad [width=3.38803615101437 height=3.79345389117291 connect=center]
  J2 = Piezo Speaker
  S1 = SWITCH-MOMENTARY-2 [package=tactile-pth]
  R1 = Resistor [tolerance=±5% resistance=220 package=THT]

nets:
  N1: J1.pin12, R1.Pin_0
  N2: J1.pin30, J2.pin1
  N3: J1.pin32, Pad11.pad
  N4: J1.pin33, Pad10.pad
  N5: J1.pin35, Pad9.pad
  N6: J1.pin38, Pad5.pad, Pad6.pad, Pad7.pad
  N7: J1.pin40, Pad1.pad, Pad2.pad, Pad3.pad
  N8: S1.1, R1.Pin_1

notes:
  +
  -
  IR Sensors
  EasyRaceLapTimer PI2 Sensor Shield Rev1
